# Fritzing sketch WeatherStation_Wiring (saved by Fritzing 0.9.3b)
breadboards: 1

parts:
  Componente1 = Arduino Uno (Rev3)
  Componente2 = BME280 Breakout
  S1 = SWITCH-MOMENTARY-2 [package=reed_switch_pth]
  S2 = SWITCH-MOMENTARY-2 [package=reed_switch_pth]
  R1 = Resistor [tolerance=±5% resistance=220 package="2512 [SMD]"]
  R2 = Resistor [tolerance=±5% resistance=220 package="0603 [SMD]"]

nets:
  N1: Componente1.A4/SDA, Componente2.SDI/SDA
  N2: Componente1.A5/SCL, Componente2.SCK/SCL
  GND: Componente1.GND, Componente2.GND
  N3: Componente1.D2, S1.1, R1.Pin_0
  N4: Componente1.D3_PWM, S2.2, R2.Pin_0
  5V: Componente1.5V, Componente2.3.3V
  N5: R1.Pin_1, R2.Pin_1

notes:
  Anemometer reed switch
  Rain gauge reed switch
